# Fritzing sketch Circuit Diagram (saved by Fritzing 0.9.3b)
breadboards: 1

parts:
  Raspberry_Pi_1 = Raspberry Pi 3 [part_number=RPI-3-V1.2]
  Servo_Motor = Basic Servo
  Power_Button = Pushbutton [package="[THT]"]
  resistor = Resistor [tolerance=±5% resistance=220 package="0805 [SMD]"]
  Oscillation_Button = Pushbutton [package="[THT]"]
  resistor_2 = Resistor [tolerance=±5% resistance=220 package="0805 [SMD]"]
  12V_DC_Fan = Fan - Ventilador [package=THT]
  TIP120_NPM_Transistor = pnp-Powertransistor [package="TO220 [THT]"]
  50V_Diode = Diode [package=diode-1n4001]
  R3 = Resistor [tolerance=±5% resistance=1k package="2512 [SMD]"]
  Sensore_PIR_HC-SR502 = HC-SR501 Body Sensor Module
  50V_Diode_2 = Diode [package=diode-1n4001]

nets:
  N1: Raspberry_Pi_1.3v3, resistor.Pin_0, resistor_2.Pin_0
  N2: Raspberry_Pi_1.GIPO4, Sensore_PIR_HC-SR502.OUT
  GND: Raspberry_Pi_1.GND, Servo_Motor.gnd, Sensore_PIR_HC-SR502.GND, 50V_Diode_2.A
  N3: Raspberry_Pi_1.GIPO5, 50V_Diode.A
  N4: Raspberry_Pi_1.GIPO26, Power_Button.Pin_1, Power_Button.Pin_2
  N5: Raspberry_Pi_1.GIPO12, Oscillation_Button.Pin_1, Oscillation_Button.Pin_2
  N6: Raspberry_Pi_1.GIPO18, Servo_Motor.pulse
  5V: Raspberry_Pi_1.5V, Servo_Motor.vcc, 12V_DC_Fan.5V, Sensore_PIR_HC-SR502.VCC
  N7: Power_Button.Pin_3, Power_Button.Pin_4, resistor.Pin_1
  N8: Oscillation_Button.Pin_3, Oscillation_Button.Pin_4, resistor_2.Pin_1
  N9: 12V_DC_Fan.GND, TIP120_NPM_Transistor.collector
  N10: TIP120_NPM_Transistor.base, R3.Pin_0

custom parts:
  Fan - Ventilador: Ventilador de 2 pines, se encuentra comunmente en computadoras de escritorio
  HC-SR501 Body Sensor Module: Pyroelectric Infrared PIR Motion Sensor Detector Module
